// Logisim project Domaci_2.circ as structural Verilog: 1 circuit, main circuit main
module main (
  input  a,
  input  b,
  input  c,
  input  d,
  input  e,
  output f
);

  wire nor_1_out, nor_2_out, nor_3_out, nor_4_out, nor_5_out, nor_6_out, nor_7_out, nor_8_out, nor_9_out;

  nor nor_1 (nor_1_out, a, b);
  nor nor_2 (nor_2_out, d, d);
  nor nor_3 (nor_3_out, e, e);
  nor nor_4 (nor_4_out, nor_2_out, nor_3_out);
  nor nor_5 (nor_5_out, nor_1_out, nor_1_out);
  nor nor_6 (nor_6_out, c, c);
  nor nor_7 (nor_7_out, nor_5_out, nor_6_out);
  nor nor_8 (nor_8_out, nor_7_out, nor_7_out);
  nor nor_9 (nor_9_out, nor_4_out, nor_4_out);
  nor nor_10 (f, nor_8_out, nor_9_out);

  // Notes on the sheet:
  //   Datum rodjenja: 13.12.
  //   1+3+1+2 = 7
  //   7 -> 00111
endmodule
